// Logisim project Trabalho arquitetura.circ as structural Verilog: 1 circuit, main circuit PC M++
module PC_M (
  input  _7,
  input  _6,
  input  _5,
  input  _4,
  input  _3,
  input  _2,
  input  _1,
  input  _0,
  input  _7_2,
  input  _6_2,
  input  _5_2,
  input  _4_2,
  input  _3_2,
  input  _2_2,
  input  _1_2,
  input  _0_2,
  input  _7_3,
  input  _6_3,
  input  _5_3,
  input  _4_3,
  input  _0_3,
  input  _1_3,
  input  _2_3,
  input  _3_3,
  input  _4_4,
  input  _5_4,
  input  _6_4,
  input  _7_4,
  input  Reset
);

  wire button_1_out, button_2_out, button_3_out, button_4_out, clock_1_out, undriven_3, undriven_4,
       undriven_5, undriven_8;
  wire [3:0] m_1_p9, m_1_p24, undriven, undriven_2;
  wire [7:0] rom_1_data, undriven_6;
  wire [15:0] undriven_7;

  // M m_1: pin names not known; wires that end beside it: _0_3, _1_3, _2_3, _3_3, _4_4, _5_4, _6_4, _7_4, m_1_p9[0], m_1_p9[1], m_1_p9[2], m_1_p9[3], _7, _6, _5, _4, _3, m_1_p24[3], _2, m_1_p24[2], _1, m_1_p24[1], _0, m_1_p24[0], _7_2, _6_2, _5_2
  Hex_Digit_Display hex_digit_display_1 (.value(m_1_p9));  // open: dp
  Hex_Digit_Display hex_digit_display_2 (.value(m_1_p24));  // open: dp
  Hex_Digit_Display hex_digit_display_3 (.value(undriven_2));  // open: dp
  Hex_Digit_Display hex_digit_display_4 (.value(undriven));  // open: dp
  Button button_1 (.out(button_1_out));
  Button button_2 (.out(button_2_out));
  Button button_3 (.out(button_3_out));
  Button button_4 (.out(button_4_out));
  Clock clock_1 (.out(clock_1_out));
  LED \Fim_de_Instrução  (.in(undriven_3));
  ROM #(.addrWidth(16)) rom_1 (.addr(undriven_7), .data(rom_1_data), .sel(undriven_8));
  RAM #(.bus("asynch")) ram_1 (.addr(undriven_6), .data(rom_1_data), .sel(undriven_4), .ld(undriven_5), .clr(Reset));

  // Notes on the sheet:
  //   + 1
  //   - 1
  //   + 1
  //   - 1
  //   ROM
  //   RAM
  //   contents of rom_1 (hex, n*v repeats v):
  //   7 c1 0 7 c9 0 7 d1 0 7 d9 0 c4 db cc d3 d4 cb dc c3 de 7 20 1 7 5 0 38 de 7 20 2 7 5 0 58 de 7 20 4
  //   7 5 0 7e de 7 20 8 7 5 0 9e 7 3 0 c c4 c 7 20 12 7 5 0 14 c4 e1 c4 7 20 a 7 5 0 4f 7 3 0 c 7 c1 0 cc
  //   e9 7 3 0 c c4 c 7 20 0 7 5 0 14 c4 7 20 0 7 5 0 72 c4 7 20 1 c1 7 3 0 c 7 c1 9 cc 7 20 1 c9 7 3 0 c
  //   d4 1c 7 20 12 7 5 0 14 d4 f1 d4 7 20 a 7 5 0 95 7 3 0 c 7 d1 0 dc f9 7 3 0 c d4 1c 7 20 0 7 5 0 14
  //   d4 7 20 0 7 5 0 b8 d4 7 20 1 d1 7 3 0 c 7 d1 9 dc 7 20 1 d9 7 3 0 c
endmodule
