// Logisim project PC.circ as structural Verilog: 1 circuit, main circuit PC M++
module PC_M (
  input  _7,
  input  _6,
  input  _5,
  input  _4,
  input  _3,
  input  _2,
  input  _1,
  input  _0,
  input  _7_2,
  input  _6_2,
  input  _5_2,
  input  _4_2,
  input  _3_2,
  input  _2_2,
  input  _1_2,
  input  _0_2,
  input  _7_3,
  input  _6_3,
  input  _5_3,
  input  _4_3,
  input  _0_3,
  input  _1_3,
  input  _2_3,
  input  _3_3,
  input  _4_4,
  input  _5_4,
  input  _6_4,
  input  _7_4,
  input  Reset
);

  wire button_1_out, button_2_out, button_3_out, button_4_out, clock_1_out, undriven_3, undriven_4,
       undriven_5, undriven_8;
  wire [3:0] m_1_p9, m_1_p24, undriven, undriven_2;
  wire [7:0] rom_1_data, undriven_6;
  wire [15:0] undriven_7;

  // M m_1: pin names not known; wires that end beside it: _0_3, _1_3, _2_3, _3_3, _4_4, _5_4, _6_4, _7_4, m_1_p9[0], m_1_p9[1], m_1_p9[2], m_1_p9[3], _7, _6, _5, _4, _3, m_1_p24[3], _2, m_1_p24[2], _1, m_1_p24[1], _0, m_1_p24[0], _7_2, _6_2, _5_2
  Hex_Digit_Display hex_digit_display_1 (.value(m_1_p9));  // open: dp
  Hex_Digit_Display hex_digit_display_2 (.value(m_1_p24));  // open: dp
  Hex_Digit_Display hex_digit_display_3 (.value(undriven_2));  // open: dp
  Hex_Digit_Display hex_digit_display_4 (.value(undriven));  // open: dp
  Button button_1 (.out(button_1_out));
  Button button_2 (.out(button_2_out));
  Button button_3 (.out(button_3_out));
  Button button_4 (.out(button_4_out));
  Clock clock_1 (.out(clock_1_out));
  LED \Fim_de_Instrução  (.in(undriven_3));
  ROM #(.addrWidth(16)) rom_1 (.addr(undriven_7), .data(rom_1_data), .sel(undriven_8));
  RAM #(.bus("asynch")) ram_1 (.addr(undriven_6), .data(rom_1_data), .sel(undriven_4), .ld(undriven_5), .clr(Reset));

  // Notes on the sheet:
  //   ROM
  //   RAM
  //   contents of rom_1 (hex, n*v repeats v):
  //   7 c0 1 e0 c1 e0 c9 e0 d1 e0 d9 7 7 3 7 7 b 7 7 13 7 7 1b 7 6 0 33 7 7 1c 7 7 14 7 7 c 7 7 4 c4 c3 cc
  //   cb d4 d3 dc db 7 3 0 2f 7 c0 0 c1 c9 d1 d9 7 7
endmodule
